# Fritzing sketch NetduinoXBee (saved by Fritzing 0.7.10b)
breadboards: 1

parts:
  Netduino1 = Netduino Plus
  Part1 = XBee Explorer Regulated

nets:
  N1: Netduino1.D1_TX0, Part1.DIN
  N2: Netduino1.D0_RX0, Part1.DOUT
  3V3: Netduino1.3V3, Part1.3.3V
  GND: Netduino1.GND, Part1.GND
