# Fritzing sketch NetduinoWirelessIntrusionDetection (saved by Fritzing 0.7.10b)
breadboards: 2

parts:
  Netduino1 = Netduino Plus
  Netduino2 = Netduino Plus
  J1 = Infrared Proximity Sensor
  U1 = XBee
  U2 = XBee

nets:
  N1: Netduino1.D1_TX0, U1.pin3
  N2: Netduino1.D0_RX0, U1.pin2
  3V3: Netduino1.3V3, U1.VCC
  GND: Netduino1.GND, U1.GND
  N3: Netduino2.D7_RTS1, J1.Vout
  N4: Netduino2.D1_TX0, U2.pin3
  N5: Netduino2.D0_RX0, U2.pin2
  3V3_2: Netduino2.3V3, U2.VCC
  +5V: Netduino2.+5V, J1.Vcc
  N6: Netduino2.GND#19, U2.GND
  N7: Netduino2.GND#20, J1.GND
